# Fritzing sketch TH (saved by Fritzing 0.9.3b)
breadboards: 1

parts:
  Часть2 = Arduino Uno (Rev3)
  LCD1602 = LCD screen
  part = LCM1602 IIC [part_number="LCM1602 IIC" chip_label="LCM1602 IIC" package="DIP (Dual Inline) [THT]"]
  R3 = Resistor [tolerance=±5% resistance=220 package=THT]
  R4 = Resistor [tolerance=±5% resistance=220 package=THT]
  R5 = Resistor [tolerance=±5% resistance=220 package=THT]
  DHT22 = DHT22 Humidity and Temperature Sensor
  R6 = Resistor [tolerance=±5% resistance=220 package=THT]
  LED1 = LED - 5mm [color="Yellow (595nm)" package="5 mm [THT]"]
  VCC1 = Battery block 9V  # not connected
  DS3231 = ZS-042 RTC Module
  MicroSD = MicroSD Card Module

nets:
  N1: Часть2.A4/SDA, part.SDA, R4.Pin_0, DS3231.SDA
  N2: Часть2.A5/SCL, part.SCL, R3.Pin_0, DS3231.SCL
  N3: Часть2.D11_PWM/MOSI, MicroSD.MOSI
  N4: Часть2.D12/MISO, MicroSD.MISO
  N5: Часть2.D13/SCK, MicroSD.SCK
  N6: Часть2.D2, R5.Pin_0, DHT22.DATA
  N7: Часть2.D3_PWM, R6.Pin_0
  N8: Часть2.D4, MicroSD.CS
  VCC: Часть2.5V, part.VCC, R3.Pin_1, R4.Pin_1, R5.Pin_1, DHT22.VDD, DS3231.VCC, MicroSD.VCC
  GND: Часть2.GND, part.GND, DHT22.GND, LED1.cathode, DS3231.GND, MicroSD.GND
  VSS: LCD1602.VSS, part.VSS
  VDD: LCD1602.VDD, part.VDD
  N9: LCD1602.V0, part.V0
  N10: LCD1602.RS, part.RS
  N11: LCD1602.R/W, part.RW
  N12: LCD1602.E, part.E
  N13: LCD1602.DB0, part.D0
  N14: LCD1602.DB1, part.D1
  N15: LCD1602.DB2, part.D2
  N16: LCD1602.DB3, part.D3
  N17: LCD1602.DB4, part.D4
  N18: LCD1602.DB5, part.D5
  N19: LCD1602.DB6, part.D6
  N20: LCD1602.DB7, part.D7
  N21: LCD1602.LED+, part.A
  N22: LCD1602.LED-, part.K
  N23: R6.Pin_1, LED1.anode

custom parts:
  LCM1602 IIC: I2C-Module to use a 1602 or 2004 LCD on with the wire.h libory Serial LCD Modul
